// Logisim project proiect.circ as structural Verilog
module main (
  input  in_1,
  input  in_2,
  input  in_3,
  input  [11:0] in_4,
  input  in_5,
  input  [11:0] in_6,
  input  in_7,
  input  in_8,
  input  in_9,
  input  in_10,
  input  in_11,
  input  in_12,
  input  in_13,
  output [11:0] out_14,
  output out_15,
  output [11:0] out_16,
  output out_17,
  output out_18,
  output out_19,
  output [11:0] out_20,
  output [11:0] out_21,
  output out_22,
  output out_23,
  output out_24,
  output out_25,
  output [11:0] out_26,
  output out_27,
  output [11:0] out_28
);

  wire afisor_pe_7_seg_1_a, afisor_pe_7_seg_1_b, afisor_pe_7_seg_1_c, afisor_pe_7_seg_1_d,
       afisor_pe_7_seg_1_e, afisor_pe_7_seg_1_f, afisor_pe_7_seg_1_g, afisor_pe_7_seg_2_a,
       afisor_pe_7_seg_2_b, afisor_pe_7_seg_2_c, afisor_pe_7_seg_2_d, afisor_pe_7_seg_2_e,
       afisor_pe_7_seg_2_f, afisor_pe_7_seg_2_g, afisor_pe_7_seg_3_a, afisor_pe_7_seg_3_b,
       afisor_pe_7_seg_3_c, afisor_pe_7_seg_3_d, afisor_pe_7_seg_3_e, afisor_pe_7_seg_3_f,
       afisor_pe_7_seg_3_g, afisor_pe_7_seg_4_a, afisor_pe_7_seg_4_b, afisor_pe_7_seg_4_c,
       afisor_pe_7_seg_4_d, afisor_pe_7_seg_4_e, afisor_pe_7_seg_4_f, afisor_pe_7_seg_4_g,
       afisor_pe_7_seg_5_a, afisor_pe_7_seg_5_b, afisor_pe_7_seg_5_c, afisor_pe_7_seg_5_d,
       afisor_pe_7_seg_5_e, afisor_pe_7_seg_5_f, afisor_pe_7_seg_5_g, afisor_pe_7_seg_6_a,
       afisor_pe_7_seg_6_b, afisor_pe_7_seg_6_c, afisor_pe_7_seg_6_d, afisor_pe_7_seg_6_e,
       afisor_pe_7_seg_6_f, afisor_pe_7_seg_6_g, afisor_pe_7_seg_7_a, afisor_pe_7_seg_7_b,
       afisor_pe_7_seg_7_c, afisor_pe_7_seg_7_d, afisor_pe_7_seg_7_e, afisor_pe_7_seg_7_f,
       afisor_pe_7_seg_7_g, button_1_out, button_2_out, button_3_out, button_4_out, button_5_out,
       button_6_out, button_7_out, button_8_out, button_9_out, button_10_out, button_11_out, button_12_out,
       button_13_out, button_14_out, button_15_out, button_16_out, button_17_out, clock_1_out, clock_2_out,
       comparator_100_1_egal, comparator_100_1_mare, comparator_100_1_mic, dipswitch_1_p2, dipswitch_2_p1,
       dn_counter_2_numar_doze, sau_1_r, si_1_r, si_2_r, unitatea_de_control_1_am, unitatea_de_control_1_at,
       unitatea_de_control_1_cf0, unitatea_de_control_1_cf1, unitatea_de_control_1_cf2,
       unitatea_de_control_1_en_reg, unitatea_de_control_1_fs, unitatea_de_control_1_rm;
  wire [3:0] bcd_to_decimal_1_mii, bcd_to_decimal_1_sute, bcd_to_decimal_1_unitati, bcd_to_decimal_1_zeci,
       bcd_to_decimal_2_sute, bcd_to_decimal_2_unitati, bcd_to_decimal_2_zeci;
  wire [11:0] mux2to1_1_f, mux2to1_2_f, registru_memorare_1_iesiri, scazator_12biti_1_diferenta,
       sumator_12biti_2_suma;

  Button button_1 (.out(button_1_out));
  Button button_2 (.out(button_2_out));
  Button button_3 (.out(button_3_out));
  Button button_4 (.out(button_4_out));
  Button button_5 (.out(button_5_out));
  Button button_6 (.out(button_6_out));
  Button button_7 (.out(button_7_out));
  Clock clock_1 (.out(clock_1_out));
  // DipSwitch #(.number(2)) dipswitch_1: pin names not known; wires that end beside it: button_2_out, dipswitch_1_p2
  Button button_8 (.out(button_8_out));
  Button button_9 (.out(button_9_out));
  Button button_10 (.out(button_10_out));
  Button button_11 (.out(button_11_out));
  Button button_12 (.out(button_12_out));
  Button button_13 (.out(button_13_out));
  Button button_14 (.out(button_14_out));
  // DipSwitch #(.number(2)) dipswitch_2: pin names not known; wires that end beside it: dipswitch_2_p1
  Unitatea_de_Control unitatea_de_control_1 (
    .START(button_1_out), .CONFIRM(button_2_out), .CANCEL(button_3_out), .RESET(button_4_out),
    .F0(button_5_out), .F1(button_6_out), .F2(button_7_out), .F3(dipswitch_1_p2),
    .ED(dn_counter_2_numar_doze), .mic(comparator_100_1_egal), .mare(comparator_100_1_mare),
    .egal(comparator_100_1_mic), .CLK(clock_1_out), .CF0(unitatea_de_control_1_cf0),
    .CF1(unitatea_de_control_1_cf1), .CF2(unitatea_de_control_1_cf2), .En_Reg(unitatea_de_control_1_en_reg),
    .EN_comp(out_17), .AM(unitatea_de_control_1_am), .AT(unitatea_de_control_1_at),
    .FS(unitatea_de_control_1_fs), .RM(unitatea_de_control_1_rm));  // open: SUMA, PD, MR
  LED led_1 (.in(unitatea_de_control_1_am));
  LED led_2 (.in(unitatea_de_control_1_at));
  LED led_3 (.in(unitatea_de_control_1_fs));
  LED led_4 (.in(unitatea_de_control_1_rm));
  // RGBLED rgbled_1: pin names not known
  // RGBLED rgbled_2: pin names not known
  Unitatea_de_Control unitatea_de_control_2 (
    .START(button_8_out), .CONFIRM(button_9_out), .CANCEL(button_10_out), .RESET(button_11_out),
    .F0(button_12_out), .F1(button_13_out), .F2(button_14_out), .F3(dipswitch_2_p1), .ED(in_8));  // open: mic, mare, egal, SUMA, CLK, CF0, CF1, CF2, En_Reg, EN_comp, AM, AT, FS, RM, PD, MR
  SI si_1 (.A(button_2_out), .B(comparator_100_1_egal), .R(si_1_r));
  Identificare_moneda identificare_moneda_1 (
    .CF0(unitatea_de_control_1_cf0), .CF1(unitatea_de_control_1_cf1), .CF2(unitatea_de_control_1_cf2),
    .ED(unitatea_de_control_1_en_reg), .NUMAR(out_14));
  Button button_15 (.out(button_15_out));
  Button button_16 (.out(button_16_out));
  Button button_17 (.out(button_17_out));
  mux2to1 mux2to1_1 (.a(out_16), .b(scazator_12biti_1_diferenta), .sel(si_1_r), .f(mux2to1_1_f));
  BCD_to_Decimal bcd_to_decimal_1 (
    .NUMAR(mux2to1_2_f), .unitati(bcd_to_decimal_1_unitati), .zeci(bcd_to_decimal_1_zeci),
    .sute(bcd_to_decimal_1_sute), .mii(bcd_to_decimal_1_mii));
  sumator_12biti sumator_12biti_1 (
    .A(out_14), .B(registru_memorare_1_iesiri), .CIN(in_1), .COUT(out_15), .SUMA(out_16));
  SAU sau_1 (.A(comparator_100_1_mare), .B(comparator_100_1_mic), .R(sau_1_r));
  Identificare_moneda identificare_moneda_2 (
    .CF0(button_15_out), .CF1(button_16_out), .CF2(button_17_out), .ED(in_7), .NUMAR(out_21));
  Clock clock_2 (.out(clock_2_out));
  Afisor_pe_7_seg afisor_pe_7_seg_1 (
    .NUMAR(bcd_to_decimal_1_unitati), .A(afisor_pe_7_seg_1_a), .B(afisor_pe_7_seg_1_b),
    .C(afisor_pe_7_seg_1_c), .D(afisor_pe_7_seg_1_d), .E(afisor_pe_7_seg_1_e), .F(afisor_pe_7_seg_1_f),
    .G(afisor_pe_7_seg_1_g));
  Afisor_pe_7_seg afisor_pe_7_seg_2 (
    .NUMAR(bcd_to_decimal_1_zeci), .A(afisor_pe_7_seg_2_a), .B(afisor_pe_7_seg_2_b), .C(afisor_pe_7_seg_2_c),
    .D(afisor_pe_7_seg_2_d), .E(afisor_pe_7_seg_2_e), .F(afisor_pe_7_seg_2_f), .G(afisor_pe_7_seg_2_g));
  Afisor_pe_7_seg afisor_pe_7_seg_3 (
    .NUMAR(bcd_to_decimal_1_sute), .A(afisor_pe_7_seg_3_a), .B(afisor_pe_7_seg_3_b), .C(afisor_pe_7_seg_3_c),
    .D(afisor_pe_7_seg_3_d), .E(afisor_pe_7_seg_3_e), .F(afisor_pe_7_seg_3_f), .G(afisor_pe_7_seg_3_g));
  Afisor_pe_7_seg afisor_pe_7_seg_4 (
    .NUMAR(bcd_to_decimal_1_mii), .A(afisor_pe_7_seg_4_a), .B(afisor_pe_7_seg_4_b), .C(afisor_pe_7_seg_4_c),
    .D(afisor_pe_7_seg_4_d), .E(afisor_pe_7_seg_4_e), .F(afisor_pe_7_seg_4_f), .G(afisor_pe_7_seg_4_g));
  Registru_memorare registru_memorare_1 (
    .INTRARI(mux2to1_1_f), .En(in_2), .CLR(in_3), .CLOCK(clock_1_out), .IESIRI(registru_memorare_1_iesiri));
  SI si_2 (.A(sau_1_r), .B(button_2_out), .R(si_2_r));
  Registru_memorare registru_memorare_2 (
    .INTRARI(sumator_12biti_2_suma), .En(in_10), .CLR(in_11), .CLOCK(clock_2_out), .IESIRI(out_26));
  sumator_12biti sumator_12biti_2 (.A(out_21), .B(out_26), .CIN(in_9), .COUT(out_22), .SUMA(sumator_12biti_2_suma));
  dn_counter dn_counter_1 (.EN_DOZE(in_12), .CLK(clock_2_out), .NUMAR_DOZE(out_27), .Nr(out_28));
  _7_Segment_Display u_7_segment_display_1 (
    .g(afisor_pe_7_seg_4_g), .f(afisor_pe_7_seg_4_f), .a(afisor_pe_7_seg_4_a), .b(afisor_pe_7_seg_4_b),
    .e(afisor_pe_7_seg_4_e), .d(afisor_pe_7_seg_4_d), .c(afisor_pe_7_seg_4_c));  // open: dp
  _7_Segment_Display u_7_segment_display_2 (
    .g(afisor_pe_7_seg_3_g), .f(afisor_pe_7_seg_3_f), .a(afisor_pe_7_seg_3_a), .b(afisor_pe_7_seg_3_b),
    .e(afisor_pe_7_seg_3_e), .d(afisor_pe_7_seg_3_d), .c(afisor_pe_7_seg_3_c), .dp(in_5));
  _7_Segment_Display u_7_segment_display_3 (
    .g(afisor_pe_7_seg_2_g), .f(afisor_pe_7_seg_2_f), .a(afisor_pe_7_seg_2_a), .b(afisor_pe_7_seg_2_b),
    .e(afisor_pe_7_seg_2_e), .d(afisor_pe_7_seg_2_d), .c(afisor_pe_7_seg_2_c));  // open: dp
  comparator_100 comparator_100_1 (
    .SUMA(registru_memorare_1_iesiri), .mic(comparator_100_1_mic), .mare(comparator_100_1_mare),
    .egal(comparator_100_1_egal));
  scazator_12biti scazator_12biti_1 (
    .A(registru_memorare_1_iesiri), .B(in_4), .BOUT(out_18), .DIFERENTA(scazator_12biti_1_diferenta));
  _7_Segment_Display u_7_segment_display_4 (
    .g(afisor_pe_7_seg_1_g), .f(afisor_pe_7_seg_1_f), .a(afisor_pe_7_seg_1_a), .b(afisor_pe_7_seg_1_b),
    .e(afisor_pe_7_seg_1_e), .d(afisor_pe_7_seg_1_d), .c(afisor_pe_7_seg_1_c));  // open: dp
  comparator_100 comparator_100_2 (.SUMA(sumator_12biti_2_suma), .mic(out_23), .mare(out_24), .egal(out_25));
  BCD_to_Decimal bcd_to_decimal_2 (
    .NUMAR(out_26), .unitati(bcd_to_decimal_2_unitati), .zeci(bcd_to_decimal_2_zeci),
    .sute(bcd_to_decimal_2_sute));  // open: mii
  scazator_12biti scazator_12biti_2 (.A(sumator_12biti_2_suma), .B(in_6), .BOUT(out_19), .DIFERENTA(out_20));
  mux2to1 mux2to1_2 (.a(registru_memorare_1_iesiri), .b(scazator_12biti_1_diferenta), .sel(si_2_r), .f(mux2to1_2_f));
  Afisor_pe_7_seg afisor_pe_7_seg_5 (
    .NUMAR(bcd_to_decimal_2_unitati), .A(afisor_pe_7_seg_5_a), .B(afisor_pe_7_seg_5_b),
    .C(afisor_pe_7_seg_5_c), .D(afisor_pe_7_seg_5_d), .E(afisor_pe_7_seg_5_e), .F(afisor_pe_7_seg_5_f),
    .G(afisor_pe_7_seg_5_g));
  Afisor_pe_7_seg afisor_pe_7_seg_6 (
    .NUMAR(bcd_to_decimal_2_zeci), .A(afisor_pe_7_seg_6_a), .B(afisor_pe_7_seg_6_b), .C(afisor_pe_7_seg_6_c),
    .D(afisor_pe_7_seg_6_d), .E(afisor_pe_7_seg_6_e), .F(afisor_pe_7_seg_6_f), .G(afisor_pe_7_seg_6_g));
  Afisor_pe_7_seg afisor_pe_7_seg_7 (
    .NUMAR(bcd_to_decimal_2_sute), .A(afisor_pe_7_seg_7_a), .B(afisor_pe_7_seg_7_b), .C(afisor_pe_7_seg_7_c),
    .D(afisor_pe_7_seg_7_d), .E(afisor_pe_7_seg_7_e), .F(afisor_pe_7_seg_7_f), .G(afisor_pe_7_seg_7_g));
  _7_Segment_Display u_7_segment_display_5 (
    .g(afisor_pe_7_seg_5_g), .f(afisor_pe_7_seg_5_f), .a(afisor_pe_7_seg_5_a), .b(afisor_pe_7_seg_5_b),
    .e(afisor_pe_7_seg_5_e), .d(afisor_pe_7_seg_5_d), .c(afisor_pe_7_seg_5_c));  // open: dp
  _7_Segment_Display u_7_segment_display_6 (
    .g(afisor_pe_7_seg_6_g), .f(afisor_pe_7_seg_6_f), .a(afisor_pe_7_seg_6_a), .b(afisor_pe_7_seg_6_b),
    .e(afisor_pe_7_seg_6_e), .d(afisor_pe_7_seg_6_d), .c(afisor_pe_7_seg_6_c));  // open: dp
  _7_Segment_Display u_7_segment_display_7 (
    .g(afisor_pe_7_seg_7_g), .f(afisor_pe_7_seg_7_f), .a(afisor_pe_7_seg_7_a), .b(afisor_pe_7_seg_7_b),
    .e(afisor_pe_7_seg_7_e), .d(afisor_pe_7_seg_7_d), .c(afisor_pe_7_seg_7_c), .dp(in_13));
  dn_counter dn_counter_2 (.EN_DOZE(si_2_r), .CLK(clock_1_out), .NUMAR_DOZE(dn_counter_2_numar_doze));  // open: Nr
endmodule

// VHDL entity Identificare_moneda, as the project stores it:
LIBRARY ieee;
USE ieee.std_logic_1164.all;

ENTITY Identificare_moneda IS
  PORT (CF0 : in std_logic; 
  	   CF1 : in std_logic; 
  	   CF2 : in std_logic;
  	   ED : in std_logic;
  	   NUMAR : out std_logic_vector (11 downto 0)
  	   );
END Identificare_moneda;


ARCHITECTURE TypeArchitecture OF Identificare_moneda IS

BEGIN

	process (CF0, CF1, CF2, ED)
	begin
			if (ED = '1') then 
				if (CF0 = '1') then 
					NUMAR <= "000000000101"; 
				elsif (CF1 = '1') then 
					NUMAR <= "000000001010"; 
				elsif (CF2 = '1') then 
					NUMAR <= "000000110010"; 
				else
					NUMAR <= "000000000000";
				end if;
			end if;
		
end process;
END TypeArchitecture;

// VHDL entity Registru_memorare, as the project stores it:
LIBRARY ieee;
USE ieee.std_logic_1164.all;

ENTITY Registru_memorare IS
  PORT (
  		INTRARI : in STD_LOGIC_VECTOR (11 downto 0);
  		En, CLR: in STD_LOGIC;
  		CLOCK : in STD_LOGIC;
  		IESIRI : out STD_LOGIC_VECTOR (11 downto 0) 
  	);
END Registru_memorare;


ARCHITECTURE arh OF Registru_memorare IS
signal M : STD_LOGIC_VECTOR (11 downto 0);

BEGIN
	process (CLOCK, CLR, INTRARI, EN)
	begin
		if rising_edge(CLOCK) then
			if (CLR = '1') then M <= x"000"; 
			else if (EN = '1') then M <= INTRARI;
				else M <= M;
				end if;
			end if;
		end if;	
	end process;
	IESIRI <= M;
END arh;

// VHDL entity sumator_12biti, as the project stores it:
--sumator pe 12 biti
LIBRARY ieee;
USE ieee.std_logic_1164.all;

ENTITY sumator_12biti IS
  PORT (
  		A : in STD_LOGIC_VECTOR (11 downto 0);
  		B : in STD_LOGIC_VECTOR (11 downto 0);
  		CIN : in STD_LOGIC;
  		COUT : out STD_LOGIC;
  		SUMA : out STD_LOGIC_VECTOR (11 downto 0)
 	 );
END sumator_12biti;

ARCHITECTURE arh OF sumator_12biti IS

COMPONENT SUMATOR IS
  PORT (
  		A,B,Cin:in std_logic;
  		Cout,S:out std_logic
  	  );
END COMPONENT;
signal N1, N2, N3, N4, N5, N6, N7, N8, N9, N10, N11 : STD_LOGIC;
BEGIN
	C1: SUMATOR port map ( A(0), B(0), CIN, N1, SUMA(0));
	C2: SUMATOR port map ( A(1), B(1), N1, N2, SUMA(1));
	C3: SUMATOR port map ( A(2), B(2), N2, N3, SUMA(2));
	C4: SUMATOR port map ( A(3), B(3), N3, N4, SUMA(3));
	C5: SUMATOR port map ( A(4), B(4), N4, N5, SUMA(4));
	C6: SUMATOR port map ( A(5), B(5), N5, N6, SUMA(5));
	C7: SUMATOR port map ( A(6), B(6), N6, N7, SUMA(6));
	C8: SUMATOR port map ( A(7), B(7), N7, N8, SUMA(7));
	C9: SUMATOR port map ( A(8), B(8), N8, N9, SUMA(8));
	C10: SUMATOR port map ( A(9), B(9), N9, N10, SUMA(9));
	C11: SUMATOR port map ( A(10), B(10), N10, N11, SUMA(10));
	C12: SUMATOR port map ( A(11), B(11), N11, COUT, SUMA(11));	
END arh;

--sumator pe 1 bit
LIBRARY ieee;
USE ieee.std_logic_1164.all;

ENTITY SUMATOR IS
  PORT (
  		A,B,Cin:in std_logic;
  		Cout,S:out std_logic
  	);
END SUMATOR;

ARCHITECTURE FluxDeDate OF SUMATOR IS

--signal V:std_logic;
BEGIN
	S <= A xor B xor Cin;
	Cout <= (A and B) or (A and Cin) or (B and Cin);  
END FluxDeDate;

// VHDL entity comparator_100, as the project stores it:
LIBRARY ieee;
USE ieee.std_logic_1164.all;
USE ieee.std_logic_unsigned.all;
USE ieee.numeric_std.all;

ENTITY comparator_100 IS
  PORT (
  		SUMA : in STD_LOGIC_VECTOR(11 downto 0);
  		mic : out STD_LOGIC;
  		mare : out STD_LOGIC;
  		egal : out STD_LOGIC	
 	  );
END comparator_100;


ARCHITECTURE arh OF comparator_100 IS

COMPONENT Convertor_VEC_in_INT IS
  PORT (A : in STD_LOGIC_VECTOR(11 downto 0);
  	   B : out INTEGER);
END COMPONENT Convertor_VEC_in_INT;

SIGNAL nr : INTEGER;

BEGIN
	C1 : Convertor_VEC_in_INT port map(SUMA,nr);
     process(nr)
     begin
         if (nr > 100) then mare <= '1'; mic <= '0'; egal <= '0';
	    elsif (nr < 100) then mic <= '1'; mare <= '0'; egal <= '0';
	       else egal <= '1'; mare <= '0'; mic <= '0';
	    end if;
     end process;
end arh;


LIBRARY ieee;
USE ieee.std_logic_1164.all;
USE ieee.std_logic_unsigned.all;
USE ieee.numeric_std.all;

ENTITY Convertor_VEC_in_INT IS
  PORT (
  		A : in STD_LOGIC_VECTOR(11 downto 0);
  	     B : out INTEGER
  	   );
END Convertor_VEC_in_INT;

ARCHITECTURE arh OF Convertor_VEC_in_INT IS
SIGNAL nr : INTEGER;
BEGIN
	B <= to_integer(unsigned(A));
end arh;

// VHDL entity Unitatea_de_Control, as the project stores it:
LIBRARY ieee;
USE ieee.std_logic_1164.all;

ENTITY Unitatea_de_Control IS
  PORT (START, CONFIRM, CANCEL : in STD_LOGIC; -- intrari user
  	   RESET, F0, F1, F2, F3, ED : in STD_LOGIC;
	   mic, mare, egal, SUMA: in STD_LOGIC; -- intrari control
	   CLK : in STD_LOGIC;
	   CF0, CF1, CF2, En_Reg, EN_comp : out STD_LOGIC;
	   AM, AT, FS, RM, PD, MR : out STD_LOGIC -- iesiri control
  	  );
END Unitatea_de_Control;

 
ARCHITECTURE TypeArchitecture OF Unitatea_de_Control IS

TYPE Stare is (Inceput, S1, S2, S3, S4, S5, S6, S7);
SIGNAL Stare_curenta, Stare_urmatoare : Stare := Inceput;

BEGIN

	--procesul de clock
	process(CLK, RESET)
	begin
		if (RESET = '1') then Stare_curenta <= Inceput;
		else
			if rising_edge(CLK) then Stare_curenta <= Stare_urmatoare; 
			end if;	
		end if;  
	end process;


	--procesul pentru iesiri si stari
	process(START, CONFIRM, CANCEL, ED, F0, F1, F2, F3)
	begin

		CF0 <= '0'; CF1 <= '0'; CF2 <= '0'; 
		AM <= '0'; AT <= '0'; FS <= '0'; RM <= '0'; PD <= '0'; MR <= '0'; EN_comp <= '0';
		
		case Stare_curenta is
			
			when Inceput => if START = '1' then En_Reg <= '1'; Stare_urmatoare <= S1;
						 else Stare_urmatoare <= Inceput;
						 end if;
			
			when S1 => if ED = '1' then Stare_urmatoare <= S2;
					 else FS <= '1'; Stare_urmatoare <= Inceput;
					 end if;
			
			when S2 => if F3 = '1' then MR <= '1'; Stare_urmatoare <= S1;
					 else 
					 	--En_reg <= '0';
					 	if F0 = '1' then CF0 <= '1'; AM <= '1';
					 	elsif F1 = '1' then CF1 <= '1'; AM <= '1'; 
					 	elsif F2 = '1' then CF2 <= '1'; AM <= '1';  
					 	end if; 
					 	
					 end if;

			when S3 => if CONFIRM = '1' then EN_comp <= '1'; AT <= '1';
					 else Stare_urmatoare <= S2;
					 end if;
					 Stare_urmatoare <= S4;

			when S4 => if mic = '1' then RM <= '1'; Stare_urmatoare <= S7;
					 else AT <= '1'; PD <= '1'; Stare_urmatoare <= S5;
					 end if;
					 
			when S5 => if CANCEL = '1' then Stare_urmatoare <= S6;
					 else 
					 	if ED = '1' then Stare_urmatoare <= S3;
					 	else FS <= '1'; Stare_urmatoare <= Inceput;
					 	end if;
					 end if;

			when S6 => if SUMA = '1' then RM <= '1'; Stare_urmatoare <= S7;
					 else Stare_urmatoare <= Inceput;
					 end if;

			when S7 => RM <= '1'; Stare_urmatoare <= Inceput;
			
		end case;
	end process;
END TypeArchitecture;

// VHDL entity scazator_12biti, as the project stores it:
--scazator pe 12 biti
LIBRARY ieee;
USE ieee.std_logic_1164.all;

ENTITY scazator_12biti IS
  PORT (
  		A : in STD_LOGIC_VECTOR (11 downto 0);
  		B : in STD_LOGIC_VECTOR (11 downto 0);
  		BOUT : out STD_LOGIC;
  		DIFERENTA : out STD_LOGIC_VECTOR (11 downto 0)
 	 );
END scazator_12biti;

ARCHITECTURE arh OF scazator_12biti IS

COMPONENT SCAZATOR IS
  PORT (
  		A,B,Bin:in std_logic;
  		Bout,D:out std_logic
  	  );
END COMPONENT;
signal N1, N2, N3, N4, N5, N6, N7, N8, N9, N10, N11 : STD_LOGIC;
BEGIN
	C1: SCAZATOR port map ( A(0), B(0), '0', N1, DIFERENTA(0));
	C2: SCAZATOR port map ( A(1), B(1), N1, N2, DIFERENTA(1));
	C3: SCAZATOR port map ( A(2), B(2), N2, N3, DIFERENTA(2));
	C4: SCAZATOR port map ( A(3), B(3), N3, N4, DIFERENTA(3));
	C5: SCAZATOR port map ( A(4), B(4), N4, N5, DIFERENTA(4));
	C6: SCAZATOR port map ( A(5), B(5), N5, N6, DIFERENTA(5));
	C7: SCAZATOR port map ( A(6), B(6), N6, N7, DIFERENTA(6));
	C8: SCAZATOR port map ( A(7), B(7), N7, N8, DIFERENTA(7));
	C9: SCAZATOR port map ( A(8), B(8), N8, N9, DIFERENTA(8));
	C10: SCAZATOR port map ( A(9), B(9), N9, N10, DIFERENTA(9));
	C11: SCAZATOR port map ( A(10), B(10), N10, N11, DIFERENTA(10));
	C12: SCAZATOR port map ( A(11), B(11), N11, BOUT, DIFERENTA(11));	
END arh;

--scazator pe 1 bit
LIBRARY ieee;
USE ieee.std_logic_1164.all;

ENTITY SCAZATOR IS
  PORT (
  		A,B,Bin:in std_logic;
  		Bout,D:out std_logic
  	);
END SCAZATOR;

ARCHITECTURE FluxDeDate OF SCAZATOR IS

signal V:std_logic;
BEGIN
	D <= A xor B xor Bin;
	Bout <= ((B xor Bin) and not(A)) or (B and Bin);
END FluxDeDate;

// VHDL entity dn_counter, as the project stores it:
library IEEE;
use IEEE.STD_LOGIC_1164.ALL;
use IEEE.STD_LOGIC_UNSIGNED.ALL;

entity dn_counter is
    Port (
           EN_DOZE : in  STD_LOGIC;
           CLK : in  STD_LOGIC; 
           NUMAR_DOZE : out  STD_LOGIC;
           Nr : out STD_LOGIC_VECTOR (11 downto 0)
            ); 
end dn_counter;

architecture Behavioral of dn_counter is
    signal count   : STD_LOGIC_VECTOR (11 downto 0) := X"00F";
    signal aux : STD_LOGIC;
begin
    process (CLK, EN_DOZE)
    begin
        if rising_edge(CLK) then
            if (EN_DOZE = '1') then
                count <= count - '1';   -- counting down
            end if;
        end if;
        if count = x"000" then aux <= '0';
        else aux <= '1';
        end if;
    end process;
    NUMAR_DOZE <= aux;  
    Nr <= count;
     
end Behavioral;

// VHDL entity mux2to1, as the project stores it:
library ieee;
use ieee.std_logic_1164.all; 

entity mux2to1 is
  port (a, b : in std_logic_vector (11 downto 0);
   		sel : in std_logic;
     	f : out std_logic_vector (11 downto 0)); 
end mux2to1;

architecture behaviour of mux2to1 is 
begin
  process (a, b, sel)
  begin
    if sel = '0' then
      f <= a;
    else
      f <= b;
    end if;
  end process;
end behaviour;

// VHDL entity BCD_to_Decimal, as the project stores it:
LIBRARY ieee;
USE ieee.std_logic_1164.all;
USE ieee.std_logic_unsigned.all;
USE ieee.std_logic_arith.all;

ENTITY BCD_to_Decimal IS
  	PORT (
	   		NUMAR : in STD_LOGIC_VECTOR (11 downto 0);
  	   		unitati : out STD_LOGIC_VECTOR (3 downto 0);
  	   		zeci : out STD_LOGIC_VECTOR (3 downto 0);
  	  	     sute : out STD_LOGIC_VECTOR (3 downto 0);
  	  	     mii : out STD_LOGIC_VECTOR (3 downto 0)
  		  );
END BCD_to_Decimal;


ARCHITECTURE TypeArchitecture OF BCD_to_Decimal IS

COMPONENT Convertor_VEC_in_INT IS
	PORT (A : in STD_LOGIC_VECTOR (11 downto 0);
		 B : out INTEGER);
END COMPONENT Convertor_VEC_in_INT;

SIGNAL q : INTEGER;
SIGNAL u, z, s, m : INTEGER := 0;
BEGIN

	C1 : Convertor_VEC_in_INT port map(NUMAR, q);
	m <= q / 1000;
	s <= q / 100;
	z <= (q / 10) rem 10;
	u <= q rem 10;	

	--proces pentru cifra unitatilor
	process(u)
	begin
		case u is
			when 0 => unitati <= x"0";
			when 1 => unitati <= x"1";
			when 2 => unitati <= x"2";
			when 3 => unitati <= x"3";
			when 4 => unitati <= x"4";
			when 5 => unitati <= x"5";
			when 6 => unitati <= x"6";
			when 7 => unitati <= x"7";
			when 8 => unitati <= x"8";
			when 9 => unitati <= x"9";
			when others => unitati <= x"f";
		end case;
	end process;

	--proces pentru cifra zecilor
	process(z)
	begin
		case z is
			when 0 => zeci <= x"0";
			when 1 => zeci <= x"1";
			when 2 => zeci <= x"2";
			when 3 => zeci <= x"3";
			when 4 => zeci <= x"4";
			when 5 => zeci <= x"5";
			when 6 => zeci <= x"6";
			when 7 => zeci <= x"7";
			when 8 => zeci <= x"8";
			when 9 => zeci <= x"9";
			when others => zeci <= x"f";
		end case;
	end process;

	--proces pentru cifra sutelor
	process(s)
	begin
		case s is
			when 0 => sute <= x"0";
			when 1 => sute <= x"1";
			when 2 => sute <= x"2";
			when 3 => sute <= x"3";
			when 4 => sute <= x"4";
			when 5 => sute <= x"5";
			when 6 => sute <= x"6";
			when 7 => sute <= x"7";
			when 8 => sute <= x"8";
			when 9 => sute <= x"9";
			when others => sute <= x"f";
		end case;
	end process; 


	--proces pentru cifra miilor
	process(m)
	begin
		case m is
			when 0 => mii <= x"0";
			when 1 => mii <= x"1";
			when 2 => mii <= x"2";
			when 3 => mii <= x"3";
			when 4 => mii <= x"4";
			when 5 => mii <= x"5";
			when 6 => mii <= x"6";
			when 7 => mii <= x"7";
			when 8 => mii <= x"8";
			when 9 => mii <= x"9";
			when others => mii <= x"f";
		end case;
	end process;

END TypeArchitecture;


--conversie din semnal in integer
LIBRARY ieee;
USE ieee.std_logic_1164.all;
USE ieee.std_logic_unsigned.all;
USE ieee.numeric_std.all;

ENTITY Convertor_VEC_in_INT IS
	PORT (A : in STD_LOGIC_VECTOR (11 downto 0);
		 B : out INTEGER);
end Convertor_VEC_in_INT;

ARCHITECTURE FLUXDEDATE OF Convertor_VEC_in_INT IS 
BEGIN
	B <= to_integer(unsigned(A));
END FLUXDEDATE;

// VHDL entity SI, as the project stores it:
LIBRARY ieee;
USE ieee.std_logic_1164.all;

ENTITY SI IS
  PORT (A : in STD_LOGIC;
  	   B : in STD_LOGIC;
  	   R : out STD_LOGIC
       );
END SI;

ARCHITECTURE TypeArchitecture OF SI IS

BEGIN
	R <= A and not(B);
END TypeArchitecture;

// VHDL entity SAU, as the project stores it:
LIBRARY ieee;
USE ieee.std_logic_1164.all;

ENTITY SAU IS
  PORT (A : in STD_LOGIC;
  	   B : in STD_LOGIC;
  	   R : out STD_LOGIC
       );
END SAU;

ARCHITECTURE TypeArchitecture OF SAU IS

BEGIN
	R <= A or B;
END TypeArchitecture;

// VHDL entity Afisor_pe_7_seg, as the project stores it:
LIBRARY ieee;
USE ieee.std_logic_1164.all;

ENTITY Afisor_pe_7_seg IS
  PORT (NUMAR : in STD_LOGIC_VECTOR(3 downto 0);
  	   A : out STD_LOGIC;
  	   B : out STD_LOGIC;
  	   C : out STD_LOGIC;
  	   D : out STD_LOGIC;
  	   E : out STD_LOGIC;
  	   F : out STD_LOGIC;
  	   G : out STD_LOGIC
);
END Afisor_pe_7_seg;

ARCHITECTURE TypeArchitecture OF Afisor_pe_7_seg IS

--COMPONENT Convertor_VEC_in_INT IS
--	PORT (A : in STD_LOGIC_VECTOR (11 downto 0);
--		 B : out INTEGER);
--END COMPONENT Convertor_VEC_in_INT;
  
BEGIN
--	C1 : Convertor_VEC_in_INT port map();
	process(NUMAR)
	begin
		case NUMAR is
			when "0000" => A<='1'; B<= '1'; C<='1'; D<='1'; E<='1'; F<='1'; G<='0'; --0
			when "0001" => A<='0'; B<= '1'; C<='1'; D<='0'; E<='0'; F<='0'; G<='0'; --1
			when "0010" => A<='1'; B<= '1'; C<='0'; D<='1'; E<='1'; F<='0'; G<='1'; --2
			when "0011" => A<='1'; B<= '1'; C<='1'; D<='1'; E<='0'; F<='0'; G<='1'; --3
			when "0100" => A<='0'; B<= '1'; C<='1'; D<='0'; E<='0'; F<='1'; G<='1'; --4
			when "0101" => A<='1'; B<= '0'; C<='1'; D<='1'; E<='0'; F<='1'; G<='1'; --5
			when "0110" => A<='1'; B<= '0'; C<='1'; D<='1'; E<='1'; F<='1'; G<='1'; --6
			when "0111" => A<='1'; B<= '1'; C<='1'; D<='0'; E<='0'; F<='0'; G<='0'; --7
			when "1000" => A<='1'; B<= '1'; C<='1'; D<='1'; E<='1'; F<='1'; G<='1'; --8
			when "1001" => A<='1'; B<= '1'; C<='1'; D<='1'; E<='0'; F<='1'; G<='1'; --9
			when others => A<='0'; B<= '0'; C<='0'; D<='0'; E<='0'; F<='0'; G<='0'; 
		end case;
	end process
;	
END TypeArchitecture;
